# Fritzing sketch ArgiCar (saved by Fritzing 0.9.10b)
breadboards: 1

parts:
  Mod1 = Amica NodeMCU DEVKIT 1.0
  M2 = Dagu DGServo 9g (Top view) [part_number=RS001B]
  KF-1 = KF-301 Relay [package=THT]
  Motor_1 = gear-motor
  Motor_2 = gear-motor
  Motor_4 = gear-motor
  Motor_3 = gear-motor
  Moisture_sensor = FC-28 Soil Hygrometer Module - Probe
  Moisture_reader = FC-28 Soil Hygrometer Module
  WATER_PUMP = water pump/motor
  Mod2 = L298N DC motor driver
  VCC1 = Battery

nets:
  N1: Mod1.pin1, Mod1.pin_10, Mod1.pin_26, M2.vcc, KF-1.power
  GND: Mod1.pin2, Mod1.pin_9, Mod1.pin_25, Mod1.pin_29, M2.gnd, KF-1.ground, Moisture_reader.GND, WATER_PUMP.pin_1, Mod2.GND, VCC1.-
  N2: Mod1.pin5, M2.pulse
  N3: Mod1.pin8, Moisture_reader.VCC
  N4: Mod1.pin_11, Mod2.IN4
  N5: Mod1.pin_12, Mod2.IN3
  N6: Mod1.pin_13, Mod2.IN2
  N7: Mod1.pin_14, Mod2.IN1
  N8: Mod1.pin_15, KF-1.signal
  N9: Mod1.pin_16, Moisture_reader.AO
  N10: Mod1.pin_30, KF-1.C, Mod2.5V, Mod2.+5V-J1, Mod2.+5V-J2
  N11: KF-1.NO, WATER_PUMP.pin_2
  N12: Motor_1.pin_1, Motor_2.pin_1, Mod2.OUT2
  N13: Motor_1.pin_2, Motor_2.pin_2, Mod2.OUT1
  N14: Motor_4.pin_1, Motor_3.pin_1, Mod2.OUT4
  N15: Motor_4.pin_2, Motor_3.pin_2, Mod2.OUT3
  N16: Moisture_sensor.POS, Moisture_reader.POS
  N17: Moisture_sensor.NEG, Moisture_reader.NEG
  N18: Mod2.12V, VCC1.+

custom parts:
  KF-301 Relay: KF-301
  FC-28 Soil Hygrometer Module - Probe: The FC-28 is a soil hygrometer module that uses the Texas Instruments LM393 comparator chip to provide an analog measurement of soil humidity.
  FC-28 Soil Hygrometer Module: The FC-28 is a soil hygrometer module that uses the Texas Instruments LM393 comparator chip to provide an analog measurement of soil humidity. The digital output is high when soil moisture is over a certain threshold, as determined by adjusting the potentiometer.
  water pump/motor: WATER PUMP BY ARDUBLOCKTR
  L298N DC motor driver: 2x DC motor driver with 78M05 positive voltage regulator (7..35 V) L298N: max 46 V, 2 A Set 5 V Enable jumper to enable 5 V regultor (needed for the L298N) and +5 V output at screw terminal or supply external +5 V at screw terminal Set ENA and/or ENB to +5 V to enable motor permanently or supply ENA and/or ENB with PWM signal IN1 and IN2 set rotation directory for motor A (OUT1/OUT2) IN2 and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
  Battery: Your standard 2x 18650 battery pack (7.4 Volts)
